# Fritzing sketch lampe_mit_akku (saved by Fritzing 0.9.2b)
circuit board: 6cm x 4cm
breadboards: 1

parts:
  BAT = Header 2 [package=jst-2-pth-ns]
  U2 = ESP8266 WiFi Module [part_number=ESP8266]
  U1 = DSN-MINI-360
  U3 = DSN-MINI-360
  OLED1 = 128x32 I2C Monochrome OLED Display
  LED-Strip = Header 3 [package=jst-3-pth]
  Bauteil1 = PowerBoost 500 Charger

nets (from the schematic view):
  N1: BAT.1, U3.VCC, LED-Strip.1, Bauteil1.VBAT
  GND: BAT.2, U2.GND#12, U2.IO15, U1.GND, U3.GND, OLED1.GND, LED-Strip.3, Bauteil1.GND
  3.3V: U2.IO0, U2.3.3V#11, U2.CHIP_EN, U1.VOUT, OLED1.3.3V
  DOUT: U2.IO2, LED-Strip.2
  SDA: U2.IO4, U3.SDA, OLED1.SDA
  SCL: U2.IO5, U3.SCL, OLED1.SCL
  5V: U1.VIN, Bauteil1.5.0V

custom parts:
  DSN-MINI-360: DC DC converter. vin > vout
  DSN-MINI-360: DC DC converter. vin > vout
  PowerBoost 500 Charger: The PowerBoost 500C is a little DC/DC boost converter module that can be powered by any 3.7V LiIon/LiPoly battery, and convert the battery output to 5.2V DC for running your 5V projects. At its heart is a TPS61090 boost converter from TI. This boost converter chip has some really nice extras such as low battery detection, 2A internal switch, synchronous conversion, excellent efficiency, and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
