# Fritzing sketch lampe_mit_akku_2 (saved by Fritzing 0.9.2b)
circuit board: 6cm x 4cm
perfboards: 1

parts:
  Bauteil1 = PowerBoost 500 Charger
  U1 = DSN-MINI-360
  U2 = ESP8266 WiFi Module [part_number=ESP8266]
  BAT = Header 2 [package=jst-2-pth-ns]
  U3 = DSN-MINI-360
  LED-Strip = Header 3 [package=jst-3-pth]

nets:
  GND: Bauteil1.GND, U1.GND, U2.GND#12, U2.IO15, BAT.2, U3.GND, LED-Strip.3
  N1: Bauteil1.VBAT, U3.VCC
  5V: Bauteil1.5.0V, U1.VIN
  3.3V: U1.VOUT, U2.IO0, U2.3.3V#11, U2.CHIP_EN
  DOUT: U2.IO2, LED-Strip.2
  SDA: U2.IO4, U3.SDA
  SCL: U2.IO5, U3.SCL
  N2: BAT.1, LED-Strip.1

custom parts:
  PowerBoost 500 Charger: The PowerBoost 500C is a little DC/DC boost converter module that can be powered by any 3.7V LiIon/LiPoly battery, and convert the battery output to 5.2V DC for running your 5V projects. At its heart is a TPS61090 boost converter from TI. This boost converter chip has some really nice extras such as low battery detection, 2A internal switch, synchronous conversion, excellent efficiency, and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
  DSN-MINI-360: DC DC converter. vin > vout
  DSN-MINI-360: DC DC converter. vin > vout
